# Fritzing sketch IAS-Sensor2 (saved by Fritzing 1.0.0rc)
circuit board: 4.68176cm x 2.57735cm
breadboards: 1

parts:
  MCU1 = Wemos Lolin32lite
  S1 = Pushbutton [package="[THT]"]
  LED1 = LED - 5mm [color="Red (633nm)" current=0.030A package="5 mm [THT]"]
  U1 = LIPO-1000mAh [package=lipo-1000]
  S2 = SPST Switch [package=switch-spdt-smd]
  U2 = AD22151 - Linear Output Magnetic Field Sensor [part_number=AD22151]
  R4 = Resistor [tolerance=±5% resistance=4.7k power=0.25W package=THT]
  R3 = Resistor [tolerance=±5% resistance=4.7k power=0.25W package=THT]
  R2 = Resistor [tolerance=±5% power=0.25W resistance=4.7k package=THT]
  R1 = Resistor [tolerance=±5% power=0.25W resistance=220 package=THT]

nets:
  N1: MCU1.pin_6, U2.TC2, R3.Pin_1
  N2: MCU1.pin_7, U2.TC1, R4.Pin_1
  N3: MCU1.pin_13, MCU1.pin_15, LED1.cathode, U1.-, U2.GND, R2.Pin_0
  N4: MCU1.pin_14, S2.P
  N5: MCU1.pin_26, S1.Pin_3, S1.Pin_4, R2.Pin_1
  N6: MCU1.pin_27, U2.TC3, R4.Pin_0, R3.Pin_0, R1.Pin_1
  N7: MCU1.pin_28, S1.Pin_1, S1.Pin_2
  N8: LED1.anode, R1.Pin_0
  N9: U1.+, S2.O

custom parts:
  Wemos Lolin32lite: Wemos Lolinlite32 wifi and blue tooth board based on the ESP-32 cpu, digital I/Os 19, analog inputs 6, clock 240mhz, Flash 4Mbytes, lipo battery charger (500ma connection broken out on breadboard but not pcb), usb.
